# Fritzing sketch akilli_ev_devre (saved by Fritzing 0.9.2b)
breadboards: 1

parts:
  Eleman1 = Arduino Uno (Rev3)
  LCD1 = LCD screen
  R1 = Rotary Potentiometer (Large) [maximum_resistance=100kΩ package=THT]
  R2 = Resistor [tolerance=±5% resistance=220 package=THT]
  Eleman2 = Bluetooth HC-06
  R3 = Resistor [tolerance=±5% resistance=10k package=THT]
  R4 = Resistor [tolerance=±5% resistance=10k package=THT]
  R5 = Photocell (LDR) [package=THT]
  LED1 = LED - 5mm [color="Red (633nm)" package="5 mm [THT]"]
  R6 = Temperature Sensor (Thermistor) [thermistor_type=NTC package=THT]  # not connected
  R7 = Resistor [tolerance=±5% resistance=330 package=THT]
  LED3 = LED - 5mm [color="Red (633nm)" package="5 mm [THT]"]
  LED4 = LED - 5mm [color="Red (633nm)" package="5 mm [THT]"]
  R8 = Resistor [tolerance=±5% resistance=330 package=THT]
  J2 = Basic Servo
  J3 = Piezo Speaker

nets:
  N1: Eleman1.A0, R3.Pin_1
  N2: Eleman1.A1, R4.Pin_0, R5.pin_0
  N3: Eleman1.D9_PWM, J2.pulse
  N4: Eleman1.D10_PWM/SS, J3.pin2
  N5: Eleman1.D11_PWM/MOSI, LCD1.E, LCD1.DB0
  N6: Eleman1.D12/MISO, LCD1.RS
  N7: Eleman1.D13/SCK, R8.Pin_0
  N8: Eleman1.D0/RX, Eleman2.TXD
  N9: Eleman1.D1/TX, Eleman2.RXD
  N10: Eleman1.D3_PWM, R7.Pin_0
  N11: Eleman1.D4, LCD1.DB7
  N12: Eleman1.D5_PWM, LCD1.DB6
  N13: Eleman1.D6_PWM, LCD1.DB5
  N14: Eleman1.D7, LCD1.DB3, LCD1.DB4
  VCC: Eleman1.5V, R1.leg1, R2.Pin_0, Eleman2.VCC, R5.pin_1, J2.vcc
  GND: Eleman1.GND, LCD1.VSS, LCD1.R/W, LCD1.LED-, R1.leg2, Eleman2.GND, R3.Pin_0, R4.Pin_1, LED1.cathode, LED3.cathode, LED4.cathode, J2.gnd, J3.pin1
  N15: LCD1.VDD, LCD1.V0, R1.wiper
  N16: LCD1.LED+, R2.Pin_1

notes:
  LDR (Işık Şiddeti Ölçer)
  Thermistor (Sıcaklık Sensörü)
  LED (Dış Aydınlatma)
  LED (İç Aydınlatma)
  Servo Motor (Kapı Açma/Kapama)
  Buzzer (Sesli Bildirim Aracı)
  LCD Ekran
  Potansiyometre (LCD Ekranın Parlaklığını Ayarlamak İçin)
  Bluetooth Sensörü
  FAN (Klima)
